# Fritzing sketch Schema (saved by Fritzing 0.9.3b)
breadboards: 2

parts:
  Part1 = Arduino Uno (Rev3)
  Q1 = NPN-Transistor [package="TO92 [THT]"]
  M1 = DC Motor
  R2 = Resistor [tolerance=±5% resistance=220 package=THT]
  YL-83_-_Control_Board1 = YL-83 Rain Sensor - Control Board
  YL-83_-_Detection_Board1 = YL-83 Rain Sensor - Detection Board
  Q2 = NPN-Transistor [package="TO92 [THT]"]
  R3 = Resistor [tolerance=±5% resistance=220 package=THT]
  DS1 = DS18B20 1-Wire Temperature Sensor Probe Cable
  YL-83_-_Control_Board2 = YL-83 Rain Sensor - Control Board
  Q3 = NPN-Transistor [package="TO92 [THT]"]
  R4 = Resistor [tolerance=±5% resistance=220 package=THT]
  YL-83_-_Control_Board3 = YL-83 Rain Sensor - Control Board
  Q4 = NPN-Transistor [package="TO92 [THT]"]
  R5 = Resistor [tolerance=±5% resistance=220 package=THT]
  YL-83_-_Control_Board4 = YL-83 Rain Sensor - Control Board
  Q5 = NPN-Transistor [package="TO92 [THT]"]
  R6 = Resistor [tolerance=±5% resistance=220 package=THT]
  DS2 = DS18B20 1-Wire Temperature Sensor Probe Cable
  DS3 = DS18B20 1-Wire Temperature Sensor Probe Cable

nets:
  N1: Part1.A0, YL-83_-_Control_Board2.AO
  N2: Part1.A1, YL-83_-_Control_Board3.AO
  N3: Part1.A2, YL-83_-_Control_Board4.AO
  N4: Part1.D10_PWM/SS, R3.Pin_1
  N5: Part1.D11_PWM/MOSI, R2.Pin_1
  N6: Part1.D2, YL-83_-_Control_Board1.DO
  VCC: Part1.5V, YL-83_-_Control_Board1.VCC, DS1.VDD, YL-83_-_Control_Board2.VCC, YL-83_-_Control_Board3.VCC, YL-83_-_Control_Board4.VCC, DS2.VDD, DS3.VDD
  GND: Part1.GND, M1.pin_1, Q2.E, DS1.GND, Q3.E, Q4.E, Q5.E, DS2.GND, DS3.GND
  N7: Part1.VIN, Q1.E
  N8: Q1.B, R2.Pin_0
  N9: Q1.C, M1.pin_2
  N10: YL-83_-_Control_Board1.GND, Q2.C
  N11: YL-83_-_Control_Board1.POS, YL-83_-_Detection_Board1.POS
  N12: YL-83_-_Control_Board1.NEG, YL-83_-_Detection_Board1.NEG
  N13: Q2.B, R3.Pin_0
  N14: DS1.shield, DS2.shield, DS3.shield
  N15: YL-83_-_Control_Board2.GND, Q3.C
  N16: Q3.B, R4.Pin_0
  N17: YL-83_-_Control_Board3.GND, Q4.C
  N18: Q4.B, R5.Pin_0
  N19: YL-83_-_Control_Board4.GND, Q5.C
  N20: Q5.B, R6.Pin_0

custom parts:
  YL-83 Rain Sensor - Control Board: The YL-83 is a rain sensor that has more resistance when dry and less resistance when wet. The module runs at 5V.
  YL-83 Rain Sensor - Detection Board: The YL-83 is a rain sensor that has more resistance when dry and less resistance when wet. The module runs at 5V.
